# Fritzing sketch bouncer (saved by Fritzing 0.5.0b)
breadboards: 1

parts:
  Arduino1 = Arduino
  R1 = Photocell (LDR) [package=THT]
  LED1 = green LED - 5mm [package="5 mm [THT]"]
  R2 = Resistor [resistance=560 package=THT]
  R3 = Resistor [resistance=10k package=THT]

nets:
  N1: Arduino1.D8, LED1.anode
  N2: Arduino1.+5V, R1.pin_1
  N3: Arduino1.GND, R2.Pin_1, R3.Pin_0
  N4: Arduino1.A0, R1.pin_0, R3.Pin_1
  N5: LED1.cathode, R2.Pin_0
