# Fritzing sketch dice (saved by Fritzing 0.3.13b)
breadboards: 1

parts:
  LED7 = Red LED - 5mm
  LED1 = Red LED - 5mm
  Arduino1 = Arduino
  R1 = Resistor [resistance=470 package=THT]
  LED2 = Red LED - 5mm
  LED3 = Red LED - 5mm
  R2 = Resistor [resistance=470 package=THT]
  R3 = Resistor [resistance=470 package=THT]
  R7 = Resistor [resistance=470 package=THT]
  LED4 = Red LED - 5mm
  LED5 = Red LED - 5mm
  LED6 = Red LED - 5mm
  R6 = Resistor [resistance=470 package=THT]
  R5 = Resistor [resistance=470 package=THT]
  R4 = Resistor [resistance=470 package=THT]
  S1 = Pushbutton [package="[THT]"]
  RPD = Resistor [resistance=10k package=THT]
  U1 = 74HC595 [package="DIP16 [THT]"]

nets:
  N1: LED7.cathode, R7.Pin_0
  N2: LED7.anode, U1.Q7
  N3: LED1.cathode, R1.Pin_1
  N4: LED1.anode, U1.Q1
  GND: Arduino1.GND, R1.Pin_0, R2.Pin_0, R3.Pin_0, R7.Pin_1, R6.Pin_1, R5.Pin_1, R4.Pin_1, S1.Pin_3, S1.Pin_4, U1.GND, U1.OE
  N5: Arduino1.D5, S1.Pin_1, S1.Pin_2, RPD.Pin_1
  N6: Arduino1.D4, LED5.anode, U1.Q5, U1.ST_CP
  N7: Arduino1.D3, U1.SH_CP
  N8: Arduino1.D2, U1.DS
  VIN: Arduino1.VIN, U1.MR, U1.VCC
  N9: LED2.cathode, R2.Pin_1
  N10: LED2.anode, U1.Q2
  N11: LED3.cathode, R3.Pin_1
  N12: LED3.anode, U1.Q3
  N13: LED4.cathode, R4.Pin_0
  N14: LED4.anode, U1.Q4
  N15: LED5.cathode, R5.Pin_0
  N16: LED6.cathode, R6.Pin_0
  N17: LED6.anode, U1.Q6
