# Fritzing sketch eitech (saved by Fritzing 0.7.1b)
breadboards: 1

parts:
  Arduino1 = Arduino
  LED_FWD = LED - 5mm [color="Red (633nm)" package="5 mm [THT]"]
  R_FWD = Resistor [tolerance=±5% resistance=560 package=THT]
  LED_RIGHT = LED - 5mm [color="Red (633nm)" package="5 mm [THT]"]
  R_RIGHT = Resistor [tolerance=±5% resistance=560 package=THT]
  LED_BACK = LED - 5mm [color="Red (633nm)" package="5 mm [THT]"]
  R_BACK = Resistor [tolerance=±5% resistance=560 package=THT]
  LED_LEFT = LED - 5mm [color="Red (633nm)" package="5 mm [THT]"]
  R_LEFT = Resistor [tolerance=±5% resistance=560 package=THT]
  LED_UP = LED - 5mm [color="Red (633nm)" package="5 mm [THT]"]
  LED_DOWN = LED - 5mm [color="Red (633nm)" package="5 mm [THT]"]
  R_DOWN = Resistor [tolerance=±5% resistance=560 package=THT]
  R_UP = Resistor [tolerance=±5% resistance=560 package=THT]

nets:
  N1: Arduino1.GND, R_FWD.Pin_1, R_RIGHT.Pin_1, R_BACK.Pin_0, R_LEFT.Pin_1, R_DOWN.Pin_0, R_UP.Pin_1
  N2: Arduino1.D9, LED_DOWN.anode
  N3: Arduino1.D8, LED_UP.anode
  N4: Arduino1.D6, LED_LEFT.anode
  N5: Arduino1.D5, LED_BACK.anode
  N6: Arduino1.D3, LED_FWD.anode
  N7: Arduino1.D2, LED_RIGHT.anode
  N8: LED_FWD.cathode, R_FWD.Pin_0
  N9: LED_RIGHT.cathode, R_RIGHT.Pin_0
  N10: LED_BACK.cathode, R_BACK.Pin_1
  N11: LED_LEFT.cathode, R_LEFT.Pin_0
  N12: LED_UP.cathode, R_UP.Pin_0
  N13: LED_DOWN.cathode, R_DOWN.Pin_1

notes:
  => To the Nunchuck
  Eitech crane stub
