# Fritzing sketch metronome (saved by Fritzing 0.5.0b)
breadboards: 1

parts:
  Arduino1 = Arduino
  R1 = Rotary Potentiometer (Small)
  S1 = Pushbutton [package="[THT]"]
  R2 = Resistor [resistance=10k package=THT]
  J1 = Piezo Speaker
  LED1 = Red LED - 5mm [package="5 mm [THT]"]
  R3 = Resistor [resistance=560 package=THT]

nets:
  N1: Arduino1.D7, S1.Pin_3, S1.Pin_4, R2.Pin_0
  N2: Arduino1.D5, J1.pin2
  N3: Arduino1.D3, LED1.anode
  N4: Arduino1.+5V, R1.leg2, R2.Pin_1
  N5: Arduino1.GND, R1.leg1, S1.Pin_1, S1.Pin_2, J1.pin1, R3.Pin_1
  N6: Arduino1.A0, R1.wiper
  N7: LED1.cathode, R3.Pin_0
