# Fritzing sketch nikon_lapse-altoids (saved by Fritzing 0.7.1b)
breadboards: 1

parts:
  Arduino = Arduino
  Stops_LED = green LED - 5mm [package="5 mm [THT]"]
  R1 = Resistor [resistance=560 tolerance=±5% package=THT]
  Thirds_LED = Red LED - 5mm [package="5 mm [THT]"]
  R2 = Resistor [resistance=560 tolerance=±5% package=THT]
  Infrared_LED = white LED - 5mm [package="5 mm [THT]"]
  R3 = Resistor [resistance=560 tolerance=±5% package=THT]
  Control = Rotary Potentiometer (Small)

nets:
  N1: Arduino.GND, R1.Pin_0, R2.Pin_0, Infrared_LED.cathode, Control.leg2
  N2: Arduino.D4, Thirds_LED.anode
  N3: Arduino.D3, Stops_LED.anode
  N4: Arduino.D2, R3.Pin_1
  N5: Arduino.+5V, Control.leg1
  N6: Arduino.A5, Control.wiper
  N7: Stops_LED.cathode, R1.Pin_1
  N8: Thirds_LED.cathode, R2.Pin_1
  N9: Infrared_LED.anode, R3.Pin_0
