# Fritzing sketch TwoServosCar (saved by Fritzing 0.3.13b)
breadboards: 1

parts:
  Arduino1 = Arduino
  VCC1 = obsolete Battery
  Trim = Trimmer Potentiometer [package=THT]
  Speed = Trimmer Potentiometer [package=THT]
  J1 = Basic Servo
  J2 = Basic Servo
  Stop = Pushbutton [package="[THT]"]
  PU = Resistor [resistance=220 package=THT]

nets:
  GND: Arduino1.GND, VCC1.-, Trim.leg2, Speed.leg2, J1.gnd, J2.gnd, Stop.Pin_3, Stop.Pin_4
  N1: Arduino1.D5, Stop.Pin_1, Stop.Pin_2, PU.Pin_1
  N2: Arduino1.D3, J1.pulse
  N3: Arduino1.D2, J2.pulse
  N4: Arduino1.+5V, Trim.leg1, Speed.leg1, PU.Pin_0
  N5: Arduino1.A4, Speed.wiper
  N6: Arduino1.A5, Trim.wiper
  VCC: VCC1.+, J1.vcc, J2.vcc
